// Logisim project Components.circ as structural Verilog: 1 circuit, main circuit Contro Unit
module Contro_Unit (
  input  in_1,
  input  [5:0] in_2,
  input  [5:0] in_3
);


  // Other names for the same wires on the sheet: CLK = in_1; Func_Code[5:0] = in_3; Op_Code[5:0] = in_2
endmodule
